// Logisim project 12BitRegister1.circ as structural Verilog: 1 circuit, main circuit main
module main (
  input  [11:0] in_1,
  input  clk,
  input  Increment,
  input  ld,
  input  clr,
  output [11:0] out_6
);

  wire or_1_out;
  wire [11:0] adder_1_out, multiplexer_1_out;

  Adder #(.width(12)) adder_1 (.a(12'h1), .b(out_6), .out(adder_1_out));  // open: cin, cout
  Multiplexer #(.width(12)) multiplexer_1 (
    .in0(in_1), .in1(adder_1_out), .out(multiplexer_1_out), .sel(Increment));  // open: en
  Register #(.width(12)) register_1 (.D(multiplexer_1_out), .en(or_1_out), .Q(out_6), .clk(clk), .clr(clr));
  or or_1 (or_1_out, Increment, ld);

  // Notes on the sheet:
  //   12 Bit Regisor
endmodule
