// Logisim project Arithematic Logical Unit.circ as structural Verilog: 1 circuit, main circuit main
module main (
  input  [15:0] DR,
  input  [1:0] Eval,
  input  CLK,
  input  [7:0] INPR,
  input  [6:0] INP_7,
  input  Inc,
  input  CLEAN,
  output E,
  output [15:0] AC
);

  wire and_1_out, d_ff_1_qn, main_1_cout, main_2_cout, main_3_cout, main_4_cout, main_5_cout, main_6_cout,
       main_7_cout, main_8_cout, main_9_cout, main_10_cout, main_11_cout, main_12_cout, main_13_cout,
       main_14_cout, main_15_cout, main_16_cout, multiplexer_3_out, multiplexer_4_out, multiplexer_5_out,
       or_1_out, or_2_out;
  wire [6:0] multiplexer_2_out;
  wire [15:0] multiplexer_1_out;

  or or_1 (or_1_out, 1'b0, multiplexer_2_out[6], multiplexer_2_out[5], multiplexer_2_out[4], multiplexer_2_out[2], multiplexer_2_out[1], multiplexer_2_out[0], multiplexer_2_out[3]);
  Multiplexer #(.width(16)) multiplexer_1 (.in0(DR), .in1(16'h1), .out(multiplexer_1_out), .sel(Inc));  // open: en
  Multiplexer #(.width(7)) multiplexer_2 (
    .in0(INP_7), .in1(7'b0000010), .out(multiplexer_2_out), .sel(Inc));  // open: en
  ALU_Block_main main_1 (
    .AND(multiplexer_2_out[0]), .ADD(multiplexer_2_out[1]), .DR(multiplexer_2_out[2]),
    .INPR(multiplexer_2_out[3]), .COM(multiplexer_2_out[4]), .SHR(multiplexer_2_out[5]),
    .SHL(multiplexer_2_out[6]), .DR_i(multiplexer_1_out[0]), .AC_i_1(AC[1]), .AC_i(AC[0]), .AC_i_1_2(E),
    .Cin(1'b0), .INPR_I(INPR[0]), .LD(or_1_out), .CLK(CLK), .Cout(main_1_cout), .AC_i_2(AC[0]), .Clear(CLEAN));
  ALU_Block_main main_2 (
    .AND(multiplexer_2_out[0]), .ADD(multiplexer_2_out[1]), .DR(multiplexer_2_out[2]),
    .INPR(multiplexer_2_out[3]), .COM(multiplexer_2_out[4]), .SHR(multiplexer_2_out[5]),
    .SHL(multiplexer_2_out[6]), .DR_i(multiplexer_1_out[1]), .AC_i_1(AC[2]), .AC_i(AC[1]), .AC_i_1_2(AC[0]),
    .Cin(main_1_cout), .INPR_I(INPR[1]), .LD(or_1_out), .CLK(CLK), .Cout(main_2_cout), .AC_i_2(AC[1]),
    .Clear(CLEAN));
  ALU_Block_main main_3 (
    .AND(multiplexer_2_out[0]), .ADD(multiplexer_2_out[1]), .DR(multiplexer_2_out[2]),
    .INPR(multiplexer_2_out[3]), .COM(multiplexer_2_out[4]), .SHR(multiplexer_2_out[5]),
    .SHL(multiplexer_2_out[6]), .DR_i(multiplexer_1_out[2]), .AC_i_1(AC[3]), .AC_i(AC[2]), .AC_i_1_2(AC[1]),
    .Cin(main_2_cout), .INPR_I(INPR[2]), .LD(or_1_out), .CLK(CLK), .Cout(main_3_cout), .AC_i_2(AC[2]),
    .Clear(CLEAN));
  ALU_Block_main main_4 (
    .AND(multiplexer_2_out[0]), .ADD(multiplexer_2_out[1]), .DR(multiplexer_2_out[2]),
    .INPR(multiplexer_2_out[3]), .COM(multiplexer_2_out[4]), .SHR(multiplexer_2_out[5]),
    .SHL(multiplexer_2_out[6]), .DR_i(multiplexer_1_out[3]), .AC_i_1(AC[4]), .AC_i(AC[3]), .AC_i_1_2(AC[2]),
    .Cin(main_3_cout), .INPR_I(INPR[3]), .LD(or_1_out), .CLK(CLK), .Cout(main_4_cout), .AC_i_2(AC[3]),
    .Clear(CLEAN));
  ALU_Block_main main_5 (
    .AND(multiplexer_2_out[0]), .ADD(multiplexer_2_out[1]), .DR(multiplexer_2_out[2]),
    .INPR(multiplexer_2_out[3]), .COM(multiplexer_2_out[4]), .SHR(multiplexer_2_out[5]),
    .SHL(multiplexer_2_out[6]), .DR_i(multiplexer_1_out[4]), .AC_i_1(AC[5]), .AC_i(AC[4]), .AC_i_1_2(AC[3]),
    .Cin(main_4_cout), .INPR_I(INPR[4]), .LD(or_1_out), .CLK(CLK), .Cout(main_5_cout), .AC_i_2(AC[4]),
    .Clear(CLEAN));
  ALU_Block_main main_6 (
    .AND(multiplexer_2_out[0]), .ADD(multiplexer_2_out[1]), .DR(multiplexer_2_out[2]),
    .INPR(multiplexer_2_out[3]), .COM(multiplexer_2_out[4]), .SHR(multiplexer_2_out[5]),
    .SHL(multiplexer_2_out[6]), .DR_i(multiplexer_1_out[5]), .AC_i_1(AC[6]), .AC_i(AC[5]), .AC_i_1_2(AC[4]),
    .Cin(main_5_cout), .INPR_I(INPR[5]), .LD(or_1_out), .CLK(CLK), .Cout(main_6_cout), .AC_i_2(AC[5]),
    .Clear(CLEAN));
  ALU_Block_main main_7 (
    .AND(multiplexer_2_out[0]), .ADD(multiplexer_2_out[1]), .DR(multiplexer_2_out[2]),
    .INPR(multiplexer_2_out[3]), .COM(multiplexer_2_out[4]), .SHR(multiplexer_2_out[5]),
    .SHL(multiplexer_2_out[6]), .DR_i(multiplexer_1_out[6]), .AC_i_1(AC[7]), .AC_i(AC[6]), .AC_i_1_2(AC[5]),
    .Cin(main_6_cout), .INPR_I(INPR[6]), .LD(or_1_out), .CLK(CLK), .Cout(main_7_cout), .AC_i_2(AC[6]),
    .Clear(CLEAN));
  ALU_Block_main main_8 (
    .AND(multiplexer_2_out[0]), .ADD(multiplexer_2_out[1]), .DR(multiplexer_2_out[2]),
    .INPR(multiplexer_2_out[3]), .COM(multiplexer_2_out[4]), .SHR(multiplexer_2_out[5]),
    .SHL(multiplexer_2_out[6]), .DR_i(multiplexer_1_out[7]), .AC_i_1(AC[8]), .AC_i(AC[7]), .AC_i_1_2(AC[6]),
    .Cin(main_7_cout), .INPR_I(INPR[7]), .LD(or_1_out), .CLK(CLK), .Cout(main_8_cout), .AC_i_2(AC[7]),
    .Clear(CLEAN));
  ALU_Block_main main_9 (
    .AND(multiplexer_2_out[0]), .ADD(multiplexer_2_out[1]), .DR(multiplexer_2_out[2]),
    .INPR(multiplexer_2_out[3]), .COM(multiplexer_2_out[4]), .SHR(multiplexer_2_out[5]),
    .SHL(multiplexer_2_out[6]), .DR_i(multiplexer_1_out[8]), .AC_i_1(AC[9]), .AC_i(AC[8]), .AC_i_1_2(AC[7]),
    .Cin(main_8_cout), .INPR_I(1'b0), .LD(or_1_out), .CLK(CLK), .Cout(main_9_cout), .AC_i_2(AC[8]),
    .Clear(CLEAN));
  ALU_Block_main main_10 (
    .AND(multiplexer_2_out[0]), .ADD(multiplexer_2_out[1]), .DR(multiplexer_2_out[2]),
    .INPR(multiplexer_2_out[3]), .COM(multiplexer_2_out[4]), .SHR(multiplexer_2_out[5]),
    .SHL(multiplexer_2_out[6]), .DR_i(multiplexer_1_out[9]), .AC_i_1(AC[10]), .AC_i(AC[9]), .AC_i_1_2(AC[8]),
    .Cin(main_9_cout), .INPR_I(1'b0), .LD(or_1_out), .CLK(CLK), .Cout(main_10_cout), .AC_i_2(AC[9]),
    .Clear(CLEAN));
  ALU_Block_main main_11 (
    .AND(multiplexer_2_out[0]), .ADD(multiplexer_2_out[1]), .DR(multiplexer_2_out[2]),
    .INPR(multiplexer_2_out[3]), .COM(multiplexer_2_out[4]), .SHR(multiplexer_2_out[5]),
    .SHL(multiplexer_2_out[6]), .DR_i(multiplexer_1_out[10]), .AC_i_1(AC[11]), .AC_i(AC[10]),
    .AC_i_1_2(AC[9]), .Cin(main_10_cout), .INPR_I(1'b0), .LD(or_1_out), .CLK(CLK), .Cout(main_11_cout),
    .AC_i_2(AC[10]), .Clear(CLEAN));
  ALU_Block_main main_12 (
    .AND(multiplexer_2_out[0]), .ADD(multiplexer_2_out[1]), .DR(multiplexer_2_out[2]),
    .INPR(multiplexer_2_out[3]), .COM(multiplexer_2_out[4]), .SHR(multiplexer_2_out[5]),
    .SHL(multiplexer_2_out[6]), .DR_i(multiplexer_1_out[11]), .AC_i_1(AC[12]), .AC_i(AC[11]),
    .AC_i_1_2(AC[10]), .Cin(main_11_cout), .INPR_I(1'b0), .LD(or_1_out), .CLK(CLK), .Cout(main_12_cout),
    .AC_i_2(AC[11]), .Clear(CLEAN));
  ALU_Block_main main_13 (
    .AND(multiplexer_2_out[0]), .ADD(multiplexer_2_out[1]), .DR(multiplexer_2_out[2]),
    .INPR(multiplexer_2_out[3]), .COM(multiplexer_2_out[4]), .SHR(multiplexer_2_out[5]),
    .SHL(multiplexer_2_out[6]), .DR_i(multiplexer_1_out[12]), .AC_i_1(AC[13]), .AC_i(AC[12]),
    .AC_i_1_2(AC[11]), .Cin(main_12_cout), .INPR_I(1'b0), .LD(or_1_out), .CLK(CLK), .Cout(main_13_cout),
    .AC_i_2(AC[12]), .Clear(CLEAN));
  ALU_Block_main main_14 (
    .AND(multiplexer_2_out[0]), .ADD(multiplexer_2_out[1]), .DR(multiplexer_2_out[2]),
    .INPR(multiplexer_2_out[3]), .COM(multiplexer_2_out[4]), .SHR(multiplexer_2_out[5]),
    .SHL(multiplexer_2_out[6]), .DR_i(multiplexer_1_out[13]), .AC_i_1(AC[14]), .AC_i(AC[13]),
    .AC_i_1_2(AC[12]), .Cin(main_13_cout), .INPR_I(1'b0), .LD(or_1_out), .CLK(CLK), .Cout(main_14_cout),
    .AC_i_2(AC[13]), .Clear(CLEAN));
  ALU_Block_main main_15 (
    .AND(multiplexer_2_out[0]), .ADD(multiplexer_2_out[1]), .DR(multiplexer_2_out[2]),
    .INPR(multiplexer_2_out[3]), .COM(multiplexer_2_out[4]), .SHR(multiplexer_2_out[5]),
    .SHL(multiplexer_2_out[6]), .DR_i(multiplexer_1_out[14]), .AC_i_1(AC[15]), .AC_i(AC[14]),
    .AC_i_1_2(AC[13]), .Cin(main_14_cout), .INPR_I(1'b0), .LD(or_1_out), .CLK(CLK), .Cout(main_15_cout),
    .AC_i_2(AC[14]), .Clear(CLEAN));
  ALU_Block_main main_16 (
    .AND(multiplexer_2_out[0]), .ADD(multiplexer_2_out[1]), .DR(multiplexer_2_out[2]),
    .INPR(multiplexer_2_out[3]), .COM(multiplexer_2_out[4]), .SHR(multiplexer_2_out[5]),
    .SHL(multiplexer_2_out[6]), .DR_i(multiplexer_1_out[15]), .AC_i_1(E), .AC_i(AC[15]), .AC_i_1_2(AC[14]),
    .Cin(main_15_cout), .INPR_I(1'b0), .LD(or_1_out), .CLK(CLK), .Cout(main_16_cout), .AC_i_2(AC[15]),
    .Clear(CLEAN));
  Multiplexer multiplexer_3 (
    .in0(multiplexer_4_out), .in1(and_1_out), .out(multiplexer_3_out), .sel(Eval[0]));  // open: en
  Multiplexer multiplexer_4 (
    .in0(multiplexer_5_out), .in1(AC[0]), .out(multiplexer_4_out), .sel(multiplexer_2_out[5]));  // open: en
  Multiplexer multiplexer_5 (
    .in0(main_16_cout), .in1(AC[15]), .out(multiplexer_5_out), .sel(multiplexer_2_out[6]));  // open: en
  D_Flip_Flop d_ff_1 (
    .clk(CLK), .D(multiplexer_3_out), .Q(E), .Qn(d_ff_1_qn), .en(or_2_out), .reset(Eval[1]));  // open: preset
  and and_1 (and_1_out, d_ff_1_qn, Eval[0]);
  or or_2 (or_2_out, Eval[0], multiplexer_2_out[5], multiplexer_2_out[6]);
endmodule
