// Logisim project Control Unit.circ as structural Verilog: 1 circuit, main circuit main
module main (
  input  AC_Val,
  input  DR,
  input  AC15,
  input  E,
  input  FGO,
  input  FGI,
  input  R_prime_T0,
  input  R_prime_T1,
  input  R_prime_T2,
  input  D7_prime_IT3,
  input  T1_prime_T2_prime_T3_prime,
  input  RT0,
  input  RT1,
  input  RT2,
  input  D0T4,
  input  D0T5,
  input  D1T4,
  input  D1T5,
  input  D2T4,
  input  D2T5,
  input  D3T4,
  input  D4T4,
  input  D5T4,
  input  D5T5,
  input  D6T4,
  input  D6T5,
  input  D6T6,
  input  rB0,
  input  rB1,
  input  rB2,
  input  rB3,
  input  rB4,
  input  rB5,
  input  rB6,
  input  rB7,
  input  rB8,
  input  rB9,
  input  rB10,
  input  rB11,
  input  pB6,
  input  pB7,
  input  pB8,
  input  pB9,
  input  pB10,
  input  pB11,
  output INC_AR,
  output LD_AR,
  output CLR_AR,
  output RJ,
  output Rk,
  output INC_PC,
  output LD_PC,
  output CLR_PC,
  output READ,
  output WRITE,
  output INC_DR,
  output LD_DR,
  output LD_IR,
  output LD_TR,
  output INC_AC,
  output CLR_AC,
  output S0,
  output S1,
  output S2,
  output S__0,
  output ADD,
  output AND,
  output DR_2,
  output INPR,
  output COM,
  output SHR,
  output SHL,
  output E__E_prime,
  output E__0,
  output SC__0,
  output IEN__0,
  output IEN__1
);

  wire not_1_out, not_2_out, not_3_out, not_4_out;
  wire [6:0] and_2_out;

  or or_1 (SC__0, pB11, pB7, pB6, rB11, rB10, rB7, rB6, rB9, rB8, rB4, rB3, rB2, rB1, D5T5, D6T6, D5T4, D4T4, D3T4, D2T5, D1T5, D0T5, pB8, pB9, pB10, pB11);
  or or_2 (IEN__0, RT2, pB6);
  not not_1 (not_1_out, DR);
  not not_2 (not_2_out, AC_Val);
  and and_1 (and_2_out[2], not_2_out, rB2);
  and and_2 (and_2_out[0], not_1_out, D6T6);
  not not_3 (not_3_out, AC15);
  not not_4 (not_4_out, E);
  and and_3 (and_2_out[3], AC15, rB3);
  and and_4 (and_2_out[4], not_3_out, rB4);
  and and_5 (and_2_out[1], not_4_out, rB1);
  and and_6 (and_2_out[5], FGO, pB8);
  and and_7 (and_2_out[6], FGI, pB9);
  or or_3 (LD_AR, R_prime_T0, R_prime_T2, D7_prime_IT3);
  or or_4 (LD_PC, D4T4, D5T5);
  or or_5 (INC_PC, RT2, R_prime_T1, and_2_out[0], and_2_out[1], and_2_out[2], and_2_out[3], and_2_out[4], and_2_out[5], and_2_out[6]);
  or or_6 (READ, R_prime_T1, D7_prime_IT3, D0T4, D1T4, D2T4, D6T4);
  or or_7 (WRITE, RT1, D3T4, D5T4, D6T6);
  or or_8 (LD_DR, D1T4, D0T4, D2T4, D6T4);
  or or_9 (S0, READ, LD_PC, D2T5, R_prime_T2, D6T6);
  or or_10 (S1, D5T4, R_prime_T0, RT0, D2T5, D6T6, READ, RT1);
  or or_11 (S2, D3T4, pB10, READ, R_prime_T2, RT1);

  assign ADD = D0T5;
  assign AND = D1T5;
  assign CLR_AC = rB11;
  assign CLR_AR = RT0;
  assign CLR_PC = RT1;
  assign COM = rB9;
  assign DR_2 = D2T5;
  assign E__0 = rB10;
  assign E__E_prime = rB8;
  assign IEN__1 = pB7;
  assign INC_AC = rB5;
  assign INC_AR = D5T4;
  assign INC_DR = D6T5;
  assign INPR = pB11;
  assign LD_IR = R_prime_T1;
  assign LD_TR = RT0;
  assign RJ = T1_prime_T2_prime_T3_prime;
  assign Rk = RT2;
  assign S__0 = rB0;
  assign SHL = rB6;
  assign SHR = rB7;
endmodule
