// Logisim project Increment Register 12.circ as structural Verilog: 1 circuit, main circuit main
module main (
  input  [11:0] INP,
  input  clock,
  input  Inc,
  input  Load,
  input  Clear,
  output [11:0] OUT
);

  wire or_1_out;
  wire [11:0] adder_1_out, multiplexer_1_out;

  Multiplexer #(.width(12)) multiplexer_1 (
    .in0(INP), .in1(adder_1_out), .out(multiplexer_1_out), .sel(Inc));  // open: en
  Adder #(.width(12)) adder_1 (.a(12'h1), .b(OUT), .out(adder_1_out));  // open: cin, cout
  or or_1 (or_1_out, Inc, Load);
  Register #(.width(12)) register_1 (.D(multiplexer_1_out), .en(or_1_out), .Q(OUT), .clk(clock), .clr(Clear));

  // Notes on the sheet:
  //   12 Bit incr Registor
endmodule
