// Logisim project Input Output Reference.circ as structural Verilog: 1 circuit, main circuit main
module main (
  input  D7IT3,
  input  [11:0] _12bit_data,
  output B6,
  output B7,
  output B8,
  output B9,
  output B10,
  output B11
);

  and and_1 (B6, D7IT3, _12bit_data[6]);
  and and_2 (B7, D7IT3, _12bit_data[7]);
  and and_3 (B8, D7IT3, _12bit_data[8]);
  and and_4 (B9, D7IT3, _12bit_data[9]);
  and and_5 (B10, D7IT3, _12bit_data[10]);
  and and_6 (B11, D7IT3, _12bit_data[11]);
endmodule
