// Logisim project Instruction Register.circ as structural Verilog: 1 circuit, main circuit main
module main (
  input  [15:0] inp,
  input  Load,
  input  Clock,
  output [15:0] out
);

  Register #(.width(16)) register_1 (.D(inp), .en(Load), .Q(out), .clk(Clock));  // open: clr

  // Notes on the sheet:
  //   Load: pull=up
endmodule
