// Logisim project Main Circuit Computer 1.circ as structural Verilog: 1 circuit, main circuit main
module main (
  input  in_1,
  input  in_2,
  input  Clear,
  input  [7:0] INPR,
  input  Inc,
  input  Clear_2,
  output E_flag
);

  wire and_1_out, and_2_out, and_3_out, Clock_out, decoder_1_out0, decoder_1_out1, decoder_1_out2,
       decoder_1_out3, decoder_1_out4, decoder_1_out5, decoder_1_out6, decoder_1_out7, FGI_q, FGO_q,
       j_k_ff_1_q, main_1_ac15, main_1_ac_val, main_1_dr_val, main_1_e_2, main_1_fgi_2, main_1_fgo_2,
       main_2_ien__0, main_2_ien__1, main_2_ld_ir, main_2_ld_tr, main_2_rj, main_2_rk, main_2_s__0,
       main_2_sc__0, not_1_out, not_2_out, not_3_out, R_flag_q, S_flag_q, SC_clear_q, Sequence_Counter_t0,
       Sequence_Counter_t1, Sequence_Counter_t2, Sequence_Counter_t3, Sequence_Counter_t4,
       Sequence_Counter_t5, Sequence_Counter_t6, Sequence_Counter_t7;
  wire [1:0] main_2_e__e_prime, main_2_inc_ac, main_2_inc_dr, main_2_read;
  wire [2:0] main_2_inc_ar, main_2_inc_pc, main_2_s0;
  wire [3:0] main_6_ac, main_6_ac_2, main_6_ac_3, main_6_ac_4, undriven, undriven_2;
  wire [5:0] main_5_b6;
  wire [6:0] main_2_add;
  wire [11:0] AR_1_out, main_3_b0, PC_2_out;
  wire [15:0] DR_3_out, IR_5_out, multiplexer_1_out, RAM_7_output, TR_6_out;
  wire [20:0] main_4_r_prime_t0;

  Sequence_Counter_main Sequence_Counter (
    .Clock(and_1_out), .Clear(SC_clear_q), .T0(Sequence_Counter_t0), .T1(Sequence_Counter_t1),
    .T2(Sequence_Counter_t2), .T3(Sequence_Counter_t3), .T4(Sequence_Counter_t4), .T5(Sequence_Counter_t5),
    .T6(Sequence_Counter_t6), .T7(Sequence_Counter_t7));
  and and_1 (and_1_out, Clock_out, not_1_out);
  not not_1 (not_1_out, S_flag_q);
  Clock Clock (.out(Clock_out));
  Value_Check_main main_1 (
    .DR(DR_3_out), .AC({main_6_ac_4, main_6_ac_3, main_6_ac_2, main_6_ac}), .E(E_flag), .FGO(FGO_q),
    .FGI(FGI_q), .DR_Val(main_1_dr_val), .AC_Val(main_1_ac_val), .AC15(main_1_ac15), .E_2(main_1_e_2),
    .FGO_2(main_1_fgo_2), .FGI_2(main_1_fgi_2));
  Decoder #(.select(3)) decoder_1 (
    .out0(decoder_1_out0), .out1(decoder_1_out1), .out2(decoder_1_out2), .out3(decoder_1_out3),
    .out4(decoder_1_out4), .out5(decoder_1_out5), .out6(decoder_1_out6), .out7(decoder_1_out7),
    .sel(IR_5_out[14:12]));  // open: en
  Control_Unit_main main_2 (
    .AC_Val(main_1_ac_val), .DR(main_1_dr_val), .AC15(main_1_ac15), .E(main_1_e_2), .FGO(main_1_fgo_2),
    .FGI(main_1_fgi_2), .R_prime_T0(main_4_r_prime_t0[0]), .R_prime_T1(main_4_r_prime_t0[1]),
    .R_prime_T2(main_4_r_prime_t0[2]), .D7_prime_IT3(main_4_r_prime_t0[3]),
    .T1_prime_T2_prime_T3_prime(main_4_r_prime_t0[4]), .RT0(main_4_r_prime_t0[5]),
    .RT1(main_4_r_prime_t0[6]), .RT2(main_4_r_prime_t0[7]), .D0T4(main_4_r_prime_t0[8]),
    .D0T5(main_4_r_prime_t0[9]), .D1T4(main_4_r_prime_t0[10]), .D1T5(main_4_r_prime_t0[11]),
    .D2T4(main_4_r_prime_t0[12]), .D2T5(main_4_r_prime_t0[13]), .D3T4(main_4_r_prime_t0[14]),
    .D4T4(main_4_r_prime_t0[15]), .D5T4(main_4_r_prime_t0[16]), .D5T5(main_4_r_prime_t0[17]),
    .D6T4(main_4_r_prime_t0[18]), .D6T5(main_4_r_prime_t0[19]), .D6T6(main_4_r_prime_t0[20]),
    .rB0(main_3_b0[0]), .rB1(main_3_b0[1]), .rB2(main_3_b0[2]), .rB3(main_3_b0[3]), .rB4(main_3_b0[4]),
    .rB5(main_3_b0[5]), .rB6(main_3_b0[6]), .rB7(main_3_b0[7]), .rB8(main_3_b0[8]), .rB9(main_3_b0[9]),
    .rB10(main_3_b0[10]), .rB11(main_3_b0[11]), .pB6(main_5_b6[0]), .pB7(main_5_b6[1]), .pB8(main_5_b6[2]),
    .pB9(main_5_b6[3]), .pB10(main_5_b6[4]), .pB11(main_5_b6[5]), .INC_AR(main_2_inc_ar[0]),
    .LD_AR(main_2_inc_ar[1]), .CLR_AR(main_2_inc_ar[2]), .RJ(main_2_rj), .Rk(main_2_rk),
    .INC_PC(main_2_inc_pc[0]), .LD_PC(main_2_inc_pc[1]), .CLR_PC(main_2_inc_pc[2]), .READ(main_2_read[0]),
    .WRITE(main_2_read[1]), .INC_DR(main_2_inc_dr[0]), .LD_DR(main_2_inc_dr[1]), .LD_IR(main_2_ld_ir),
    .LD_TR(main_2_ld_tr), .INC_AC(main_2_inc_ac[0]), .CLR_AC(main_2_inc_ac[1]), .S0(main_2_s0[0]),
    .S1(main_2_s0[1]), .S2(main_2_s0[2]), .S__0(main_2_s__0), .ADD(main_2_add[0]), .AND(main_2_add[1]),
    .DR_2(main_2_add[2]), .INPR(main_2_add[3]), .COM(main_2_add[4]), .SHR(main_2_add[5]),
    .SHL(main_2_add[6]), .E__E_prime(main_2_e__e_prime[0]), .E__0(main_2_e__e_prime[1]),
    .SC__0(main_2_sc__0), .IEN__0(main_2_ien__0), .IEN__1(main_2_ien__1));
  not not_2 (not_2_out, IR_5_out[15]);
  and and_2 (and_2_out, not_2_out, decoder_1_out7, Sequence_Counter_t3);
  and and_3 (and_3_out, decoder_1_out7, IR_5_out[15], Sequence_Counter_t3);
  Register_Reference_main main_3 (
    ._12bit_data(IR_5_out[11:0]), .D7I_prime_T3(and_2_out), .B0(main_3_b0[0]), .B1(main_3_b0[1]),
    .B2(main_3_b0[2]), .B3(main_3_b0[3]), .B4(main_3_b0[4]), .B5(main_3_b0[5]), .B6(main_3_b0[6]),
    .B7(main_3_b0[7]), .B8(main_3_b0[8]), .B9(main_3_b0[9]), .B10(main_3_b0[10]), .B11(main_3_b0[11]));
  J_K_Flip_Flop R_flag (.J(main_2_rj), .clk(and_1_out), .K(main_2_rk), .Q(R_flag_q));  // open: Qn, preset, en, reset
  D_Flip_Flop S_flag (.clk(and_1_out), .D(main_2_s__0), .Q(S_flag_q));  // open: Qn, preset, en, reset
  J_K_Flip_Flop SC_clear (
    .J(main_2_sc__0), .clk(and_1_out), .K(not_3_out), .Q(SC_clear_q));  // open: Qn, preset, en, reset
  not not_3 (not_3_out, main_2_sc__0);
  J_K_Flip_Flop j_k_ff_1 (
    .J(main_2_ien__0), .clk(and_1_out), .K(main_2_ien__1), .Q(j_k_ff_1_q));  // open: Qn, preset, en, reset
  D_Flip_Flop FGO (.clk(and_1_out), .D(in_1), .Q(FGO_q));  // open: Qn, preset, en, reset
  D_Flip_Flop FGI (.clk(and_1_out), .D(in_2), .Q(FGI_q));  // open: Qn, preset, en, reset
  Memory_Reference_main main_4 (
    .T0(Sequence_Counter_t0), .T1(Sequence_Counter_t1), .T2(Sequence_Counter_t2), .T3(Sequence_Counter_t3),
    .T4(Sequence_Counter_t4), .T5(Sequence_Counter_t5), .T6(Sequence_Counter_t6), .T7(Sequence_Counter_t7),
    .D0(decoder_1_out0), .D1(decoder_1_out1), .D2(decoder_1_out2), .D3(decoder_1_out3), .D4(decoder_1_out4),
    .D5(decoder_1_out5), .D6(decoder_1_out6), .D7(decoder_1_out7), .R(R_flag_q), .IEN(j_k_ff_1_q),
    .FGI(in_2), .FGO(in_1), .S(S_flag_q), .E(E_flag), .I(IR_5_out[15]), .R_prime_T0(main_4_r_prime_t0[0]),
    .R_prime_T1(main_4_r_prime_t0[1]), .R_prime_T2(main_4_r_prime_t0[2]),
    .D7_prime_IT3(main_4_r_prime_t0[3]), .T0_prime_T1_prime_T2_prime_IEN__FGO_FGI(main_4_r_prime_t0[4]),
    .RT0(main_4_r_prime_t0[5]), .RT1(main_4_r_prime_t0[6]), .RT2(main_4_r_prime_t0[7]),
    .D0T4(main_4_r_prime_t0[8]), .D0T5(main_4_r_prime_t0[9]), .D1T4(main_4_r_prime_t0[10]),
    .D1T5(main_4_r_prime_t0[11]), .D2T4(main_4_r_prime_t0[12]), .D2T5(main_4_r_prime_t0[13]),
    .D3T4(main_4_r_prime_t0[14]), .D4T4(main_4_r_prime_t0[15]), .D5T4(main_4_r_prime_t0[16]),
    .D5T5(main_4_r_prime_t0[17]), .D6T4(main_4_r_prime_t0[18]), .D6T5(main_4_r_prime_t0[19]),
    .D6T6(main_4_r_prime_t0[20]));
  Input_Output_Reference_main main_5 (
    ._12bit_data(IR_5_out[11:0]), .D7IT3(and_3_out), .B6(main_5_b6[0]), .B7(main_5_b6[1]), .B8(main_5_b6[2]),
    .B9(main_5_b6[3]), .B10(main_5_b6[4]), .B11(main_5_b6[5]));
  Arithematic_Logical_Unit_main main_6 (
    .DR(DR_3_out), .INPR(INPR), .INP_7(main_2_add), .Eval(main_2_e__e_prime), .Inc(main_2_inc_ac[0]),
    .CLEAN(main_2_inc_ac[1]), .CLK(and_1_out), .E(E_flag),
    .AC({main_6_ac_4, main_6_ac_3, main_6_ac_2, main_6_ac}));
  Memory_main RAM_7 (
    .Address(AR_1_out), .Data(multiplexer_1_out), .Write(main_2_read[1]), .Clock(and_1_out),
    .Read(main_2_read[0]), .OUTPUT(RAM_7_output));
  Increment_Register_12_main AR_1 (
    .INP(multiplexer_1_out[11:0]), .Inc(main_2_inc_ar[0]), .Load(main_2_inc_ar[1]), .Clear(main_2_inc_ar[2]),
    .OUT(AR_1_out), .clock(and_1_out));
  Increment_Register_12_main PC_2 (
    .INP(multiplexer_1_out[11:0]), .Inc(main_2_inc_pc[0]), .Load(main_2_inc_pc[1]), .Clear(main_2_inc_pc[2]),
    .OUT(PC_2_out), .clock(and_1_out));
  Increment_Register_16_main DR_3 (
    .INP(multiplexer_1_out), .Inc(main_2_inc_dr[0]), .Load(main_2_inc_dr[1]), .Clear(Clear), .OUT(DR_3_out),
    .Clock(and_1_out));
  Instruction_Register_main IR_5 (.inp(multiplexer_1_out), .Load(main_2_ld_ir), .Clock(and_1_out), .out(IR_5_out));
  Increment_Register_16_main TR_6 (
    .INP(multiplexer_1_out), .Inc(Inc), .Load(main_2_ld_tr), .Clear(Clear_2), .OUT(TR_6_out),
    .Clock(and_1_out));
  Multiplexer #(.select(3), .width(16)) multiplexer_1 (
    .in1({undriven, AR_1_out}), .in2({undriven_2, PC_2_out}), .in3(DR_3_out),
    .in4({main_6_ac_4, main_6_ac_3, main_6_ac_2, main_6_ac}), .in5(IR_5_out), .in6(TR_6_out),
    .in7(RAM_7_output), .out(multiplexer_1_out), .sel(main_2_s0));  // open: in0, en
  Hex_Digit_Display hex_digit_display_1 (.value(undriven));  // open: dp
  Hex_Digit_Display hex_digit_display_2 (.value(undriven_2));  // open: dp
  Hex_Digit_Display hex_digit_display_3 (.value(DR_3_out[15:12]));  // open: dp
  Hex_Digit_Display hex_digit_display_4 (.value(main_6_ac_4));  // open: dp
  Hex_Digit_Display hex_digit_display_5 (.value(IR_5_out[15:12]));  // open: dp
  Hex_Digit_Display hex_digit_display_6 (.value(AR_1_out[11:8]));  // open: dp
  Hex_Digit_Display hex_digit_display_7 (.value(AR_1_out[7:4]));  // open: dp
  Hex_Digit_Display hex_digit_display_8 (.value(PC_2_out[11:8]));  // open: dp
  Hex_Digit_Display hex_digit_display_9 (.value(PC_2_out[7:4]));  // open: dp
  Hex_Digit_Display hex_digit_display_10 (.value(DR_3_out[7:4]));  // open: dp
  Hex_Digit_Display hex_digit_display_11 (.value(DR_3_out[11:8]));  // open: dp
  Hex_Digit_Display hex_digit_display_12 (.value(main_6_ac_3));  // open: dp
  Hex_Digit_Display hex_digit_display_13 (.value(main_6_ac_2));  // open: dp
  Hex_Digit_Display hex_digit_display_14 (.value(IR_5_out[7:4]));  // open: dp
  Hex_Digit_Display hex_digit_display_15 (.value(IR_5_out[11:8]));  // open: dp
  Hex_Digit_Display hex_digit_display_16 (.value(AR_1_out[3:0]));  // open: dp
  Hex_Digit_Display hex_digit_display_17 (.value(PC_2_out[3:0]));  // open: dp
  Hex_Digit_Display hex_digit_display_18 (.value(DR_3_out[3:0]));  // open: dp
  Hex_Digit_Display hex_digit_display_19 (.value(main_6_ac));  // open: dp
  Hex_Digit_Display hex_digit_display_20 (.value(IR_5_out[3:0]));  // open: dp

  // Notes on the sheet:
  //   AR
  //   PC
  //   DR
  //   AC
  //   IR
endmodule
