// Logisim project Memory Reference.circ as structural Verilog: 1 circuit, main circuit main
module main (
  input  T0,
  input  T1,
  input  T2,
  input  T3,
  input  T4,
  input  T5,
  input  T6,
  input  T7,
  input  D0,
  input  D1,
  input  D2,
  input  D3,
  input  D4,
  input  D5,
  input  D6,
  input  D7,
  input  R,
  input  IEN,
  input  FGI,
  input  FGO,
  input  S,
  input  E,
  input  I,
  output R_prime_T0,
  output R_prime_T1,
  output R_prime_T2,
  output D7_prime_IT3,
  output T0_prime_T1_prime_T2_prime_IEN__FGO_FGI,
  output RT0,
  output RT1,
  output RT2,
  output D0T4,
  output D0T5,
  output D1T4,
  output D1T5,
  output D2T4,
  output D2T5,
  output D3T4,
  output D4T4,
  output D5T4,
  output D5T5,
  output D6T4,
  output D6T5,
  output D6T6
);

  wire not_1_out, not_2_out, not_3_out, not_4_out, not_5_out, or_1_out;

  not not_1 (not_1_out, T0);
  not not_2 (not_2_out, T1);
  not not_3 (not_3_out, T2);
  not not_4 (not_4_out, R);
  not not_5 (not_5_out, D7);
  or or_1 (or_1_out, FGO, FGI);
  and and_1 (R_prime_T0, T0, not_4_out);
  and and_2 (R_prime_T1, T1, not_4_out);
  and and_3 (R_prime_T2, T2, not_4_out);
  and and_4 (D7_prime_IT3, not_5_out, I, T3);
  and and_5 (T0_prime_T1_prime_T2_prime_IEN__FGO_FGI, IEN, not_3_out, not_2_out, not_1_out, or_1_out);
  and and_6 (RT0, T0, R);
  and and_7 (RT1, T1, R);
  and and_8 (RT2, T2, R);
  and and_9 (D0T4, D0, T4);
  and and_10 (D0T5, D0, T5);
  and and_11 (D1T4, D1, T4);
  and and_12 (D1T5, D1, T5);
  and and_13 (D2T4, D2, T4);
  and and_14 (D2T5, D2, T5);
  and and_15 (D3T4, D3, T4);
  and and_16 (D4T4, D4, T4);
  and and_17 (D5T4, D5, T4);
  and and_18 (D5T5, D5, T5);
  and and_19 (D6T4, D6, T4);
  and and_20 (D6T5, D6, T5);
  and and_21 (D6T6, D6, T6);
endmodule
