// Logisim project Memory.circ as structural Verilog: 1 circuit, main circuit main
module main (
  input  [11:0] Address,
  input  [15:0] Data,
  input  Write,
  input  Read,
  input  Clock,
  output [15:0] OUTPUT
);

  RAM #(.addrWidth(12), .dataWidth(16), .bus("separate")) ram_1 (
    .addr(Address), .din(Data), .data(OUTPUT), .str(Write), .clk(Clock), .ld(Read));  // open: sel, clr

  // Notes on the sheet:
  //   Memory
endmodule
