// Logisim project Sequence Counter.circ as structural Verilog: 1 circuit, main circuit main
module main (
  input  Clock,
  input  Clear,
  output T0,
  output T1,
  output T2,
  output T3,
  output T4,
  output T5,
  output T6,
  output T7
);

  wire [2:0] counter_1_q;

  Counter #(.width(3), .max('h7)) counter_1 (.Q(counter_1_q), .clk(Clock), .clr(Clear));  // open: load, D, count, carry
  Decoder #(.select(3)) decoder_1 (
    .out0(T0), .out1(T1), .out2(T2), .out3(T3), .out4(T4), .out5(T5), .out6(T6), .out7(T7), .sel(counter_1_q));  // open: en

  // Notes on the sheet:
  //   Sequence Counter
endmodule
